// Logisim project Lab_Prakt_2.circ as structural Verilog
module upcl (
  input  C6,
  input  C5,
  input  C4,
  input  C3,
  input  C2,
  input  C1,
  input  C0,
  output C6_2,
  output C5_2,
  output C4_2,
  output C3_2,
  output C2_2,
  output C1_2,
  output C0_2
);

  wire not_1_out, not_2_out, not_3_out, not_4_out, not_6_out;

  not not_1 (not_1_out, C6);
  not not_2 (not_2_out, C4);
  or or_1 (C4_2, C0, C3);
  not not_3 (not_3_out, C6);
  not not_4 (not_4_out, C4);
  not not_5 (C2_2, C6);
  not not_6 (not_6_out, C2);
  not not_7 (C0_2, C1);
  or or_2 (C6_2, not_1_out, not_2_out);
  or or_3 (C3_2, not_3_out, not_4_out);
  and and_1 (C1_2, not_6_out, C0);

  assign C5_2 = 1'b1;
endmodule

module Dwcl (
  input  C6,
  input  C5,
  input  C4,
  input  C3,
  input  C2,
  input  C1,
  input  C0,
  output C6_2,
  output C5_2,
  output C4_2,
  output C3_2,
  output C2_2,
  output C1_2,
  output C0_2
);

  wire and_2_out, not_2_out, not_3_out, not_5_out, not_6_out, not_8_out;

  not not_1 (C6_2, C2);
  not not_2 (not_2_out, C4);
  not not_3 (not_3_out, C0);
  not not_4 (C3_2, C2);
  not not_5 (not_5_out, C2);
  not not_6 (not_6_out, C1);
  not not_7 (C1_2, C0);
  not not_8 (not_8_out, C2);
  or or_1 (C4_2, not_2_out, not_3_out, C1);
  and and_1 (C2_2, not_5_out, not_6_out);
  and and_2 (and_2_out, C3, not_8_out);
  or or_2 (C0_2, C1, and_2_out);

  assign C5_2 = 1'b1;
endmodule
