// Logisim project D_FF.circ as structural Verilog: 2 circuits, main circuit main
module main (
  input  D,
  input  E,
  input  C,
  output Q
);

  wire nand_1_out, nand_2_out, nand_3_out, nand_4_out, nand_5_out, nand_6_out, nand_7_out;

  nand nand_1 (nand_1_out, Q, Q);
  nand nand_2 (nand_2_out, E, E);
  nand nand_3 (nand_3_out, C, C);
  nand nand_4 (nand_4_out, D, nand_1_out);
  nand nand_5 (nand_5_out, nand_2_out, Q);
  nand nand_6 (nand_6_out, nand_3_out, Q);
  nand nand_7 (nand_7_out, D, E, C);
  nand nand_8 (Q, nand_4_out, nand_5_out, nand_6_out, nand_7_out);
endmodule

module test (
  input  D,
  input  E,
  input  C,
  output Q
);

  wire nand_1_out, nand_2_out, nand_3_out, nand_4_out, nand_5_out;

  nand nand_1 (nand_1_out, E, E);
  nand nand_2 (nand_2_out, C, C);
  nand nand_3 (nand_3_out, D, E, C);
  nand nand_4 (nand_4_out, Q, nand_1_out);
  nand nand_5 (nand_5_out, Q, nand_2_out);
  nand nand_6 (Q, nand_3_out, nand_4_out, nand_5_out);
endmodule
