// Logisim project Make_Circuit_Symetric.circ as structural Verilog: 1 circuit, main circuit main
module main (
  input  A1,
  input  S1,
  input  B1,
  input  A2,
  input  S2,
  input  B2,
  output out_7,
  output out_8
);

  wire and_1_out, and_2_out, and_3_out, and_4_out, nor_1_out, nor_2_out, not_1_out;

  not not_1 (not_1_out, S1);
  and and_1 (and_1_out, A1, not_1_out);
  and and_2 (and_2_out, S1, B1);
  nor nor_1 (nor_1_out, A2, nor_2_out);
  nor nor_2 (nor_2_out, nor_1_out, B2);
  or or_1 (out_7, and_1_out, and_2_out);
  and and_3 (and_3_out, nor_1_out, S2);
  and and_4 (and_4_out, S2, nor_2_out);
  or or_2 (out_8, and_3_out, and_4_out);
endmodule
