// Logisim project Subblock_Full_Adder_Half_Adder.circ as structural Verilog: 1 circuit, main circuit main
module main (
  input  [7:0] in_1,
  input  [7:0] in_2,
  input  [7:0] in_3,
  input  [7:0] in_4,
  input  [7:0] in_5,
  input  [7:0] in_6,
  input  [7:0] in_7,
  input  [7:0] in_8,
  output [7:0] out_9,
  output [7:0] out_10,
  output [7:0] out_11,
  output [7:0] out_12
);

  wire adder_1_cout, adder_2_cout, adder_3_cout;

  Adder adder_1 (.a(in_1), .b(in_2), .out(out_9), .cout(adder_1_cout));  // open: cin
  Adder adder_2 (.a(in_3), .b(in_4), .out(out_10), .cin(adder_1_cout), .cout(adder_2_cout));
  Adder adder_3 (.a(in_5), .b(in_6), .out(out_11), .cin(adder_2_cout), .cout(adder_3_cout));
  Adder adder_4 (.a(in_7), .b(in_8), .out(out_12), .cin(adder_3_cout));  // open: cout
endmodule
