// Logisim project FSM_first_implementation.circ as structural Verilog: 7 circuits, main circuit main
module main (
);

  wire clk_out, clock_1_out, fsm_bh_1_out_basuka_hamster, fsm_bh_1_out_green, fsm_bh_1_out_red,
       fsm_bh_1_out_yellow, fsm_edge_indep_1_green, fsm_edge_indep_1_red, fsm_edge_indep_1_yellow,
       I_Button_2_out, I_Button_out, I_Sensor_out;

  Button I_Button (.out(I_Button_out));
  Clock clk (.out(clk_out));
  Button I_Button_2 (.out(I_Button_2_out));
  Button I_Sensor (.out(I_Sensor_out));
  Clock clock_1 (.out(clock_1_out));
  fsm_edge_indep fsm_edge_indep_1 (
    .Button(I_Button_out), .clk(clk_out), .Red(fsm_edge_indep_1_red), .Yellow(fsm_edge_indep_1_yellow),
    .Green(fsm_edge_indep_1_green));
  LED Red (.in(fsm_edge_indep_1_red));
  LED Yellow (.in(fsm_edge_indep_1_yellow));
  LED Green (.in(fsm_edge_indep_1_green));
  LED Red_2 (.in(fsm_bh_1_out_red));
  fsm_bh fsm_bh_1 (
    .Button(I_Button_2_out), .clk(clock_1_out), .Sensor(I_Sensor_out), .Out_Red(fsm_bh_1_out_red),
    .Out_Yellow(fsm_bh_1_out_yellow), .Out_Green(fsm_bh_1_out_green),
    .Out_Basuka_Hamster(fsm_bh_1_out_basuka_hamster));
  LED Yellow_2 (.in(fsm_bh_1_out_yellow));
  LED Green_2 (.in(fsm_bh_1_out_green));
  LED Basuka_Hamster (.in(fsm_bh_1_out_basuka_hamster));
endmodule

module fsm (
  input  Button,
  input  clk,
  output Out_Red,
  output Out_Yellow,
  output Out_Green
);

  wire fsm_tl_1_d0, fsm_tl_1_d1, state_Register_2_q, stateRegister_1_q;

  fsm_tl fsm_tl_1 (.B(Button), .C1(stateRegister_1_q), .C0(state_Register_2_q), .D1(fsm_tl_1_d1), .D0(fsm_tl_1_d0));
  D_Flip_Flop stateRegister_1 (.D(fsm_tl_1_d1), .clk(clk), .Q(stateRegister_1_q));  // open: Qn, preset, reset
  D_Flip_Flop state_Register_2 (.D(fsm_tl_1_d0), .clk(clk), .Q(state_Register_2_q));  // open: Qn, preset, reset
  fsm_ol fsm_ol_1 (
    .C1(stateRegister_1_q), .C0(state_Register_2_q), .Red(Out_Red), .Yellow(Out_Yellow), .Green(Out_Green));
endmodule

module fsm_edge_indep (
  input  Button,
  input  clk,
  output Red,
  output Yellow,
  output Green
);

  wire and_1_out, D_FF2_2_q, D_FF2_q, D_FF4_q, fsm_tl_1_d0, fsm_tl_1_d1, not_1_out;

  D_Flip_Flop D_FF2 (.D(Button), .clk(clk), .Q(D_FF2_q));  // open: Qn, preset, reset
  not not_1 (not_1_out, D_FF2_q);
  and and_1 (and_1_out, Button, not_1_out);
  fsm_tl fsm_tl_1 (.B(and_1_out), .C1(D_FF2_2_q), .C0(D_FF4_q), .D1(fsm_tl_1_d1), .D0(fsm_tl_1_d0));
  D_Flip_Flop D_FF2_2 (.D(fsm_tl_1_d1), .clk(clk), .Q(D_FF2_2_q));  // open: Qn, preset, reset
  D_Flip_Flop D_FF4 (.D(fsm_tl_1_d0), .clk(clk), .Q(D_FF4_q));  // open: Qn, preset, reset
  fsm_ol fsm_ol_1 (.C1(D_FF2_2_q), .C0(D_FF4_q), .Red(Red), .Yellow(Yellow), .Green(Green));
endmodule

module fsm_bh (
  input  Button,
  input  clk,
  input  Sensor,
  output Out_Red,
  output Out_Yellow,
  output Out_Green,
  output Out_Basuka_Hamster
);

  wire and_1_out, d_ff_1_q, d_ff_2_q, d_ff_3_q, fsm_tl_1_d0, fsm_tl_1_d1, not_1_out;

  D_Flip_Flop d_ff_1 (.D(Button), .clk(clk), .Q(d_ff_1_q));  // open: Qn, preset, reset
  not not_1 (not_1_out, d_ff_1_q);
  and and_1 (and_1_out, Button, not_1_out);
  fsm_tl fsm_tl_1 (.B(and_1_out), .C1(d_ff_2_q), .C0(d_ff_3_q), .D1(fsm_tl_1_d1), .D0(fsm_tl_1_d0));
  D_Flip_Flop d_ff_2 (.D(fsm_tl_1_d1), .clk(clk), .Q(d_ff_2_q));  // open: Qn, preset, reset
  D_Flip_Flop d_ff_3 (.D(fsm_tl_1_d0), .clk(clk), .Q(d_ff_3_q));  // open: Qn, preset, reset
  fsm_ol_bh fsm_ol_bh_1 (
    .S(Sensor), .C1(d_ff_2_q), .C0(d_ff_3_q), .Red(Out_Red), .Yellow(Out_Yellow), .Green(Out_Green),
    .BH(Out_Basuka_Hamster));
endmodule

module fsm_tl (
  input  B,
  input  C1,
  input  C0,
  output D1,
  output D0
);

  wire and_1_out, and_2_out, not_1_out, not_2_out, not_3_out;

  not not_1 (not_1_out, C1);
  not not_2 (not_2_out, C0);
  not not_3 (not_3_out, C0);
  and and_1 (and_1_out, not_1_out, C0);
  and and_2 (and_2_out, C1, not_2_out);
  and and_3 (D0, B, not_3_out);
  or or_1 (D1, and_1_out, and_2_out);
endmodule

module fsm_ol (
  input  C1,
  input  C0,
  output Red,
  output Yellow,
  output Green
);

  wire not_1_out, not_2_out;

  not not_1 (not_1_out, C1);
  not not_2 (not_2_out, C0);
  and and_1 (Green, not_1_out, not_2_out);

  assign Red = C1;
  assign Yellow = C0;
endmodule

module fsm_ol_bh (
  input  S,
  input  C1,
  input  C0,
  output Red,
  output Yellow,
  output Green,
  output BH
);

  wire not_1_out, not_2_out, not_3_out;

  not not_1 (not_1_out, C1);
  not not_2 (not_2_out, C0);
  not not_3 (not_3_out, C0);
  and and_1 (Green, not_1_out, not_2_out);
  and and_2 (BH, S, C1, not_3_out);

  assign Red = C1;
  assign Yellow = C0;
endmodule
